// Logisim project aiAlu.circ as structural Verilog: 8 circuits, main circuit Half Adder
module Half_Adder (
  input  A,
  input  B,
  output S,
  output C
);

  xor xor_1 (S, A, B);
  and and_1 (C, A, B);
endmodule

module Full_Adder (
  input  C0,
  input  A,
  input  B,
  output S,
  output C1
);

  wire and_1_out, and_2_out, and_3_out, xor_1_out;

  xor xor_1 (xor_1_out, B, A);
  xor xor_2 (S, xor_1_out, C0);
  and and_1 (and_1_out, A, C0);
  and and_2 (and_2_out, B, A);
  and and_3 (and_3_out, B, C0);
  or or_1 (C1, and_1_out, and_2_out, and_3_out);
endmodule

module aiLogic (
  input  [7:0] in_1,
  input  [7:0] in_2
);
endmodule

module a_b (
  input  [7:0] in_1,
  input  [7:0] in_2,
  output [7:0] out_3
);

  and and_1 (out_3[7], in_2[7], in_1[7]);
  and and_2 (out_3[4], in_2[4], in_1[4]);
  and and_3 (out_3[6], in_2[6], in_1[6]);
  and and_4 (out_3[5], in_2[5], in_1[5]);
  and and_5 (out_3[2], in_2[2], in_1[2]);
  and and_6 (out_3[1], in_2[1], in_1[1]);
  and and_7 (out_3[3], in_2[3], in_1[3]);
  and and_8 (out_3[0], in_2[0], in_1[0]);
endmodule

module a__b (
  input  [7:0] in_1,
  input  [7:0] in_2,
  output [7:0] out_3
);

  or or_1 (out_3[7], in_2[7], in_1[7]);
  or or_2 (out_3[5], in_2[5], in_1[5]);
  or or_3 (out_3[6], in_2[6], in_1[6]);
  or or_4 (out_3[4], in_2[4], in_1[4]);
  or or_5 (out_3[3], in_2[3], in_1[3]);
  or or_6 (out_3[1], in_2[1], in_1[1]);
  or or_7 (out_3[2], in_2[2], in_1[2]);
  or or_8 (out_3[0], in_2[0], in_1[0]);
endmodule

module notA (
  input  [7:0] in_1,
  output [7:0] out_2
);

  not not_1 (out_2[7], in_1[7]);
  not not_2 (out_2[5], in_1[5]);
  not not_3 (out_2[3], in_1[3]);
  not not_4 (out_2[6], in_1[6]);
  not not_5 (out_2[1], in_1[1]);
  not not_6 (out_2[4], in_1[4]);
  not not_7 (out_2[2], in_1[2]);
  not not_8 (out_2[0], in_1[0]);
endmodule

module notB (
  input  [7:0] in_1,
  output [7:0] out_2
);

  not not_1 (out_2[7], in_1[7]);
  not not_2 (out_2[6], in_1[6]);
  not not_3 (out_2[4], in_1[4]);
  not not_4 (out_2[1], in_1[1]);
  not not_5 (out_2[3], in_1[3]);
  not not_6 (out_2[0], in_1[0]);
  not not_7 (out_2[2], in_1[2]);
  not not_8 (out_2[5], in_1[5]);
endmodule

module AxorB (
  input  [7:0] in_1,
  input  [7:0] in_2,
  output [7:0] out_3
);

  xor xor_1 (out_3[7], in_2[7], in_1[7]);
  xor xor_2 (out_3[4], in_2[4], in_1[4]);
  xor xor_3 (out_3[5], in_2[5], in_1[5]);
  xor xor_4 (out_3[6], in_2[6], in_1[6]);
  xor xor_5 (out_3[3], in_2[3], in_1[3]);
  xor xor_6 (out_3[1], in_2[1], in_1[1]);
  xor xor_7 (out_3[2], in_2[2], in_1[2]);
  xor xor_8 (out_3[0], in_2[0], in_1[0]);
endmodule
